# Fritzing sketch shift-register-exercise-1 (saved by Fritzing 0.9.2b)
breadboards: 1

parts:
  Part1 = Arduino Pro Mini v13
  U1 = 74HC595 SMD [package="SO16 [SMD]"]
  LED1 = smd LED [color="Red (633nm)" package="1206 [SMD]"]
  LED2 = smd LED [color="Red (633nm)" package="1206 [SMD]"]
  LED3 = smd LED [color="Red (633nm)" package="1206 [SMD]"]
  LED4 = smd LED [color="Red (633nm)" package="1206 [SMD]"]
  LED5 = smd LED [color="Red (633nm)" package="1206 [SMD]"]
  LED6 = smd LED [color="Red (633nm)" package="1206 [SMD]"]
  LED7 = smd LED [color="Red (633nm)" package="1206 [SMD]"]
  LED8 = smd LED [color="Red (633nm)" package="1206 [SMD]"]
  VCC1 = Battery

nets:
  N1: Part1.RAW, VCC1.+
  GND: Part1.GND, U1.GND, U1.OE, LED1.anode, LED2.anode, LED3.anode, LED4.anode, LED5.anode, LED6.anode, LED7.anode, LED8.anode, VCC1.-
  N2: Part1.D6_PWM, U1.SH_CP
  N3: Part1.D5_PWM, U1.ST_CP
  N4: Part1.D4, U1.DS
  N5: U1.Q1, LED1.cathode
  N6: U1.Q2, LED3.cathode
  N7: U1.Q3, LED4.cathode
  N8: U1.Q4, LED5.cathode
  N9: U1.Q5, LED6.cathode
  N10: U1.Q6, LED7.cathode
  N11: U1.Q7, LED8.cathode
  N12: U1.MR, U1.VCC
  N13: U1.Q0, LED2.cathode
