# Fritzing sketch shift-register-exercise-2 (saved by Fritzing 0.9.2b)
breadboards: 2

parts:
  Part1 = Arduino Pro Mini v13
  U1 = 74HC595 SMD [package="SO16 [SMD]"]
  LED1 = smd LED [color="Red (633nm)" package="1206 [SMD]"]
  LED2 = smd LED [color="Red (633nm)" package="1206 [SMD]"]
  LED3 = smd LED [color="Red (633nm)" package="1206 [SMD]"]
  LED4 = smd LED [color="Red (633nm)" package="1206 [SMD]"]
  LED5 = smd LED [color="Red (633nm)" package="1206 [SMD]"]
  LED6 = smd LED [color="Red (633nm)" package="1206 [SMD]"]
  LED7 = smd LED [color="Red (633nm)" package="1206 [SMD]"]
  LED8 = smd LED [color="Red (633nm)" package="1206 [SMD]"]
  VCC1 = Battery
  U2 = 74HC595 SMD [package="SO16 [SMD]"]
  LED9 = smd LED [color="Red (633nm)" package="1206 [SMD]"]
  LED10 = smd LED [color="Red (633nm)" package="1206 [SMD]"]
  LED11 = smd LED [color="Red (633nm)" package="1206 [SMD]"]
  LED12 = smd LED [color="Red (633nm)" package="1206 [SMD]"]
  LED13 = smd LED [color="Red (633nm)" package="1206 [SMD]"]
  LED14 = smd LED [color="Red (633nm)" package="1206 [SMD]"]
  LED15 = smd LED [color="Red (633nm)" package="1206 [SMD]"]
  LED16 = smd LED [color="Red (633nm)" package="1206 [SMD]"]

nets:
  N1: Part1.RAW, VCC1.+
  GND: Part1.GND, U1.GND, U1.OE, LED1.anode, LED2.anode, LED3.anode, LED4.anode, LED5.anode, LED6.anode, LED7.anode, LED8.anode, VCC1.-, LED9.anode, LED10.anode, LED11.anode, LED12.anode, LED13.anode, LED14.anode, LED15.anode, LED16.anode
  VCC: Part1.VCC, U1.MR, U1.VCC
  N2: Part1.D6_PWM, U1.SH_CP, U2.OE
  N3: Part1.D5_PWM, U1.ST_CP
  N4: Part1.D4, U1.DS
  N5: U1.Q1, LED1.cathode
  N6: U1.Q2, LED3.cathode
  N7: U1.Q3, LED4.cathode
  N8: U1.Q4, LED5.cathode
  N9: U1.Q5, LED6.cathode
  N10: U1.Q6, LED7.cathode
  N11: U1.Q7, LED8.cathode
  N12: U1.Q7', U2.DS
  N13: U1.Q0, LED2.cathode
  N14: U2.Q1, LED10.cathode
  N15: U2.Q2, LED11.cathode
  N16: U2.Q3, LED12.cathode
  N17: U2.Q4, LED13.cathode
  N18: U2.Q5, LED14.cathode
  N19: U2.Q6, LED15.cathode
  N20: U2.Q7, LED16.cathode
  N21: U2.Q0, LED9.cathode
